# Fritzing sketch ESP32_NTPClock (saved by Fritzing 0.9.4)
breadboards: 1

parts:
  Part1 = ESP32 Huzzah Breakout [part_number="Adafruit #4172"]
  Part2 = Adafruit Micro USB Breakout [part_number="Adafruit #1833"]
  7SEG1 = 7-Segment LED I2C Backpack (red)

nets:
  GND: Part1.GND, Part2.GND, 7SEG1.GND
  N1: Part1.3.3V, 7SEG1.V+
  N2: Part1.GPIO23, 7SEG1.SDA
  N3: Part1.GPIO22, 7SEG1.SCL
  N4: Part1.VBAT, Part2.VBUS

custom parts:
  ESP32 Huzzah Breakout: Squeeeeze down your next ESP32 project to its bare-bones essential with the Adafruit HUZZAH32 Breakout. This breakout is basically the 'big sister' of our HUZZAH 8266, but instead of an ESP8266 it has the '32! We've pared down our popular Feather ESP32, removing the battery charger and USB-serial converter. You just get a regulator, some protection diodes, two buttons and an LED. For some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
  Adafruit Micro USB Breakout: Simple but effective - this breakout board has a USB Micro-B connector, with all 5 pins broken out. Great for pairing with a microcontroller with USB support, or adding USB 5V power to a project. We use a micro-AB connector with through-hole shielding pads for an excellent strong connection - it won't rip off by accident! Comes with one fully assembled and tested micro B breakout PCB and a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
  7-Segment LED I2C Backpack (red): 4-digit, 7-segment LED Display with I2C Control
